# Fritzing sketch bm019_iso28560_serial (saved by Fritzing 0.9.10b)
breadboards: 1

parts:
  U1 = BM01 [package=THT]
  Part1 = Arduino Uno (Rev3)
  LED1 = LED - 5mm [color="Yellow (595nm)" current=0.030 package="5 mm [THT]"]
  LED2 = LED - 5mm [color="Green (560nm)" current=0.030 package="5 mm [THT]"]
  LED3 = LED - 5mm [color="Red (633nm)" current=0.030 package="5 mm [THT]"]
  R1 = Resistor [tolerance=±5% power=0.25 resistance=330 package=THT]
  R2 = Resistor [tolerance=±5% power=0.25 resistance=330 package=THT]
  R3 = Resistor [tolerance=±5% power=0.25 resistance=330 package=THT]
  R4 = Resistor [tolerance=±5% power=0.25 resistance=1k package=THT]
  R5 = Resistor [tolerance=±5% power=0.25 resistance=1k package=THT]
  R6 = Resistor [tolerance=±5% power=0.25 resistance=1k package=THT]
  R7 = Resistor [tolerance=±5% power=0.25 resistance=1k package=THT]
  R8 = Resistor [tolerance=±5% power=0.25 resistance=2.2k package=THT]
  R9 = Resistor [tolerance=±5% power=0.25 resistance=2.2k package=THT]
  R10 = Resistor [tolerance=±5% power=0.25 resistance=2.2k package=THT]
  R11 = Resistor [tolerance=±5% power=0.25 resistance=2.2k package=THT]

nets:
  N1: U1.DIN, R7.Pin_0, R11.Pin_1
  N2: U1.SS, R6.Pin_0, R10.Pin_1
  N3: U1.MISO, Part1.D12/MISO
  N4: U1.MOSI, R5.Pin_0, R9.Pin_1
  N5: U1.SCK, R4.Pin_0, R8.Pin_1
  N6: U1.SSO, U1.VDD
  VIN: U1.VIN, Part1.5V
  GND: U1.GND, Part1.GND, R1.Pin_1, R2.Pin_1, R3.Pin_1, R8.Pin_0, R10.Pin_0, R11.Pin_0
  N7: Part1.D9_PWM, R7.Pin_1
  N8: Part1.D10_PWM/SS, R6.Pin_1
  N9: Part1.D11_PWM/MOSI, R5.Pin_1
  N10: Part1.D13/SCK, R4.Pin_1
  N11: Part1.D5_PWM, LED3.anode
  N12: Part1.D6_PWM, LED2.anode
  N13: Part1.D7, LED1.anode
  N14: LED1.cathode, R1.Pin_0
  N15: LED2.cathode, R2.Pin_0
  N16: LED3.cathode, R3.Pin_0

custom parts:
  BM01: MB019
